# Fritzing sketch DS3231_Arduino_UNO (saved by Fritzing 0.9.3b)

parts:
  ZS-042_RTC1 = ZS-042 RTC Module
  Part1 = Arduino Uno (Rev3) - ICSP

nets:
  GND: ZS-042_RTC1.GND, Part1.GND
  VCC: ZS-042_RTC1.VCC, Part1.5V
  N1: ZS-042_RTC1.SDA, Part1.A4/SDA
  N2: ZS-042_RTC1.SCL, Part1.A5/SCL
  N3: ZS-042_RTC1.SQW, Part1.D2
